# Fritzing sketch twingo-sony (saved by Fritzing 0.9.3b)
circuit board: 4.9cm x 5.2cm
breadboards: 1

parts:
  D1 = Rectifier Diode [part_number=1N4001 package="300 mil [THT]"]
  to_Twingo_Remote = female pin header, 6 pins [form="♀ (female)"]
  Tip = female pin header, 1 pin [form="♀ (female)"]
  Ring = female pin header, 1 pin [form="♀ (female)"]
  Sleeve = female pin header, 1 pin [form="♀ (female)"]
  R5 = Resistor [tolerance=±5% resistance=22k package=THT]
  R4 = Resistor [tolerance=±5% resistance=15k package=THT]
  R3 = Resistor [tolerance=±5% resistance=2.2k package=THT]
  Nano = Arduino Nano v2.3
  R1 = Resistor [tolerance=±5% resistance=1.2k package=THT]
  Voice_Conrol = IC, SIP package, 7 pins [chip_label=Reed]
  Vol_- = IC, SIP package, 7 pins [chip_label=Reed]
  4_Vol_+ = IC, SIP package, 7 pins [chip_label=Reed]
  Source = IC, SIP package, 7 pins [chip_label=Reed]
  Mute = IC, SIP package, 7 pins [chip_label=Reed]
  Off = IC, SIP package, 7 pins [chip_label=Reed]
  Preset_- = IC, SIP package, 7 pins [chip_label=Reed]
  Preset_+ = IC, SIP package, 7 pins [chip_label=Reed]
  R6 = Resistor [tolerance=±5% resistance=8.2k package=THT]
  D3 = Rectifier Diode [part_number=1N4001 package="300 mil [THT]"]
  R7 = Resistor [tolerance=±5% resistance=5.6k package=THT]
  R2 = Resistor [tolerance=±5% resistance=4.7k package=THT]
  D6 = Rectifier Diode [part_number=1N4001 package="300 mil [THT]"]
  D7 = Rectifier Diode [part_number=1N4001 package="300 mil [THT]"]
  D8 = Rectifier Diode [part_number=1N4001 package="300 mil [THT]"]
  D9 = Rectifier Diode [part_number=1N4001 package="300 mil [THT]"]

nets:
  N1: D1.cathode, Preset_-.pin1, D7.cathode
  N2: D1.anode, R6.Pin_0
  N3: to_Twingo_Remote.pin1, Nano.D7
  N4: to_Twingo_Remote.pin2, Nano.D6
  N5: to_Twingo_Remote.pin3, Nano.D5
  N6: to_Twingo_Remote.pin4, Nano.D4
  N7: to_Twingo_Remote.pin5, Nano.D3
  N8: to_Twingo_Remote.pin6, Nano.D2
  N9: Tip.pin1, R5.Pin_1, R4.Pin_1, R3.Pin_1, Nano.GND, R1.Pin_1, Voice_Conrol.pin5, Vol_-.pin5, 4_Vol_+.pin5, Source.pin5, Mute.pin5, Off.pin5, Preset_-.pin5, Preset_+.pin5, R6.Pin_1, R7.Pin_1, R2.Pin_1, D8.anode
  N10: Ring.pin1, D6.anode, D7.anode, D9.anode
  N11: Sleeve.pin1, Voice_Conrol.pin7, Vol_-.pin7, 4_Vol_+.pin7, Source.pin7, Mute.pin7, Off.pin7, Preset_-.pin7, Preset_+.pin7
  N12: R5.Pin_0, Vol_-.pin1
  N13: R4.Pin_0, 4_Vol_+.pin1
  N14: R3.Pin_0, Source.pin1
  N15: Nano.D10, Preset_+.pin3
  N16: Nano.D11, Preset_-.pin3
  N17: Nano.A5, Voice_Conrol.pin3
  N18: Nano.A4, Vol_-.pin3
  N19: Nano.A3, 4_Vol_+.pin3
  N20: Nano.A2, Source.pin3
  N21: Nano.A1, Mute.pin3
  N22: Nano.A0, Off.pin3
  N23: R1.Pin_0, Off.pin1
  N24: Voice_Conrol.pin1, D8.cathode, D9.cathode
  N25: Mute.pin1, R2.Pin_0
  N26: Preset_+.pin1, D3.cathode, D6.cathode
  N27: D3.anode, R7.Pin_0

notes:
  from http://jvde.net/comment/150
  1,2K = source/2 sec. off
  3,3k = ATT (mute)
  5,6K = display (song tag info/RDS,...)
  8,2K = tune up/next track
  12K = tune down/previous track
  15K = volume up +
  22K = volume down -
  56K = band/escape
  8,2K + SHIFT = preset up/folder up
  12K + SHIFT = preset down/folder down
  3,5mm to head unit jack
  Arduino powered via USB
  1,2K = brown-red-red
  2,2k = red-red-red
  3,3K = orange-orange-red
  8,2K = grey-red-red
  12K = brown-red-orange
  15K = brown-green-orange
  22K = red-red-orange
  220 = red-red-brown
  Comus Relays 5V
  Part number
  3570-1331-053
  OWN SETUP
  BUTTON RESISTOR HU FUNCTION
  top left 1,2k standby/off
  top right Diode voice control
  bottom 2,2K source
  vol + 15K vol +
  mute 4,7K mute
  vol - 22K vol -
  wheel up 5,6k + Diode radio: preset +
  wheel dn 8,2k + Diode radio: preset -
  from RM-X2S Sony Remote
  0 Ω Off
  2.2k Ω Source
  4.4k Ω Mute
  6.6k Ω List(Disp)
  8.8k Ω Seek up
  12.1k Ω Seek down
  16.8k Ω Volume up
  23.6k Ω Volume down
  33.6k Ω Select
  48.6k Ω Mode
